# Fritzing sketch TireTempPRO (saved by Fritzing 0.9.3b)

parts:
  0x1B = MLX90614 [package=to-39]
  0x1D = MLX90614 [package=to-39]
  0x1C = MLX90614 [package=to-39]
  Arduino_Uno_R3 = Arduino Uno (Rev3)
  0x3C_(I2C_OLED) = Grove OLED 128x96

nets:
  N1: 0x1B.SCL_VZ, 0x1D.SCL_VZ, 0x1C.SCL_VZ, Arduino_Uno_R3.A5/SCL, 0x3C_(I2C_OLED).SCL
  N2: 0x1B.PWM_SDA, 0x1D.PWM_SDA, 0x1C.PWM_SDA, Arduino_Uno_R3.A4/SDA, 0x3C_(I2C_OLED).SDA
  VDD: 0x1B.VDD, 0x1D.VDD, 0x1C.VDD, Arduino_Uno_R3.5V, 0x3C_(I2C_OLED).VCC
  VSS: 0x1B.VSS, 0x1D.VSS, 0x1C.VSS, Arduino_Uno_R3.GND, 0x3C_(I2C_OLED).GND
